// Logisim project CPU.circ as structural Verilog: 8 circuits, main circuit COMPUTER
module COMPUTER (
);

  wire BTN_RST_out, CLK, cpu_1_inta, interrupt_interface_4_1_p4, interrupt_interface_4_1_p5,
       interrupt_interface_4_1_p6, interrupt_interface_4_1_p7, pull_resistor_1_node, pull_resistor_6_node,
       ram_1_out_8, rst;
  wire [1:0] cpu_1_uext1__0;
  wire [3:0] interrupt_interface_4_1_p1;
  wire [7:0] pull_resistor_2_node, ram_1_out_7;
  wire [15:0] pull_resistor_3_node;

  Button BTN_RST (.out(BTN_RST_out));
  Clock u_CLK (.out(CLK));
  // RisingEdge risingedge_1: pin names not known; wires that end beside it: BTN_RST_out, CLK, rst
  RAM ram_1 (
    .in_1(pull_resistor_3_node), .in_2(CLK), .in_3(pull_resistor_2_node), .in_4(pull_resistor_1_node),
    .in_5(pull_resistor_6_node), .in_6(rst), .out_7(ram_1_out_7), .out_8(ram_1_out_8));
  Pull_Resistor pull_resistor_1 (.node(pull_resistor_1_node));
  Pull_Resistor pull_resistor_2 (.node(pull_resistor_2_node));
  Pull_Resistor pull_resistor_3 (.node(pull_resistor_3_node));
  Pull_Resistor pull_resistor_4 (.node(ram_1_out_7));
  Pull_Resistor pull_resistor_5 (.node(ram_1_out_8));
  Pull_Resistor pull_resistor_6 (.node(pull_resistor_6_node));
  CPU cpu_1 (
    .in_1(rst), .in_2(CLK), .in_3(ram_1_out_8), .in_4(ram_1_out_7), .ABUS(pull_resistor_3_node),
    .DOUTBUS(pull_resistor_2_node), .out_8(pull_resistor_1_node), .out_9(pull_resistor_6_node),
    .inta(cpu_1_inta), .intr3__0(interrupt_interface_4_1_p1), .UEXT1__0(cpu_1_uext1__0));
  // INTERRUPT_INTERFACE_4 interrupt_interface_4_1: pin names not known; wires that end beside it: interrupt_interface_4_1_p1, cpu_1_inta, cpu_1_uext1__0, interrupt_interface_4_1_p4, interrupt_interface_4_1_p5, interrupt_interface_4_1_p6, interrupt_interface_4_1_p7, CLK
  Button BTN_INTR3 (.out(interrupt_interface_4_1_p4));
  Button BTN_INTR2 (.out(interrupt_interface_4_1_p5));
  Button BTN_INTR1 (.out(interrupt_interface_4_1_p6));
  Button BTN_INTR0 (.out(interrupt_interface_4_1_p7));
endmodule

module CPU (
  input  in_1,
  input  in_2,
  input  in_3,
  input  [7:0] in_4,
  input  [3:0] intr3__0,
  output [15:0] ABUS,
  output [7:0] DOUTBUS,
  output out_8,
  output out_9,
  output inta,
  output [1:0] UEXT1__0
);

  wire C16, ldIVTP;
  wire [3:0] common_1_phaseffbus;
  wire [6:0] common_1_addrbus, pull_resistor_1_node;
  wire [7:0] pull_resistor_7_node;
  wire [14:0] pull_resistor_4_node, pull_resistor_6_node;
  wire [15:0] A, ALU, B, INTRADDR, PSW;
  wire [20:0] common_1_instrucbus;

  COMMON common_1 (
    .CLK(in_2), .RST(in_1), .DIN(in_4), .CMEMBUS(pull_resistor_4_node), .MAR(ABUS), .MDR(DOUTBUS),
    .PHASEFFBUS(common_1_phaseffbus), .INSTRUCBUS(common_1_instrucbus), .ADDRBUS(common_1_addrbus),
    .PSW(PSW), .CREGBUS(pull_resistor_6_node), .CFFBUS(pull_resistor_7_node), .B(B), .A(A),
    .CPSW(pull_resistor_1_node), .ALU(ALU), .IVTPPDSP(INTRADDR), .in_11(C16));
  Pull_Resistor pull_resistor_1 (.node(pull_resistor_1_node));
  Pull_Resistor pull_resistor_2 (.node(common_1_phaseffbus));
  Pull_Resistor pull_resistor_3 (.node(common_1_instrucbus));
  Pull_Resistor pull_resistor_4 (.node(pull_resistor_4_node));
  Pull_Resistor pull_resistor_5 (.node(common_1_addrbus));
  Pull_Resistor pull_resistor_6 (.node(pull_resistor_6_node));
  Pull_Resistor pull_resistor_7 (.node(pull_resistor_7_node));
  FETCH fetch_1 (
    .in_1(in_1), .in_2(in_2), .in_3(in_3), .PHASEFFBUS(common_1_phaseffbus),
    .INSTRUCBUS(common_1_instrucbus), .ADDRBUS(common_1_addrbus), .PSW(PSW), .rdMEM(out_9),
    .CMEMBUS(pull_resistor_4_node), .CFFBUS(pull_resistor_7_node), .CREGBUS(pull_resistor_6_node));
  ADDR addr_1 (
    .in_1(in_1), .in_2(in_2), .in_3(in_3), .PHASEFFBUS(common_1_phaseffbus),
    .INSTRUCBUS(common_1_instrucbus), .ADDRBUS(common_1_addrbus), .rdMEM(out_9),
    .CMEMBUS(pull_resistor_4_node), .CFFBUS(pull_resistor_7_node), .CREGBUS(pull_resistor_6_node));
  EXEC exec_1 (
    .in_1(in_1), .in_2(in_2), .in_3(in_3), .B(B), .PHASEFFBUS(common_1_phaseffbus),
    .INSTRUCBUS(common_1_instrucbus), .ADDRBUS(common_1_addrbus), .PSW(PSW), .A(A), .ALU(ALU),
    .CMEMBUS(pull_resistor_4_node), .CFFBUS(pull_resistor_7_node), .CREGBUS(pull_resistor_6_node),
    .CPSW(pull_resistor_1_node), .rdMEM(out_9), .wrMEM(out_8), .ldIVTP(ldIVTP), .C16(C16));
  INTR intr_1 (
    .in_1(in_1), .in_2(in_2), .in_3(in_3), .PHASEFFBUS(common_1_phaseffbus),
    .INSTRUCBUS(common_1_instrucbus), .PSW(PSW), .intr(intr3__0), .ADDIVTP(INTRADDR),
    .CMEMBUS(pull_resistor_4_node), .CFFBUS(pull_resistor_7_node), .CREGBUS(pull_resistor_6_node),
    .rdMEM(out_9), .wrMEM(out_8), .UEXT1__0(UEXT1__0), .inta(inta), .in_9(ldIVTP), .A15__0(A));

  // Other names for the same wires on the sheet: CLK = in_2; DIN7__0[7:0] = in_4; FCBUS = in_3; MAR[15:0] = ABUS;
  //   MDR[7:0] = DOUTBUS; RD = out_9; rst = in_1; WR = out_8
endmodule

module COMMON (
  input  CLK,
  input  [15:0] ALU,
  input  RST,
  input  [7:0] DIN,
  input  [15:0] A,
  input  [15:0] IVTPPDSP,
  input  [14:0] CMEMBUS,
  input  [7:0] CFFBUS,
  input  [14:0] CREGBUS,
  input  [6:0] CPSW,
  input  in_11,
  output [15:0] MAR,
  output [7:0] MDR,
  output [3:0] PHASEFFBUS,
  output [20:0] INSTRUCBUS,
  output [6:0] ADDRBUS,
  output [15:0] PSW,
  output [15:0] B
);

  wire adrinst, and_1_out, and_2_out, and_3_out, and_4_out, and_5_out, and_6_out, and_7_out, and_8_out,
       and_9_out, and_10_out, and_11_out, and_12_out, and_13_out, and_14_out, and_15_out, and_16_out,
       and_17_out, and_18_out, and_19_out, and_20_out, and_21_out, and_24_out, and_25_out, and_26_out,
       and_27_out, bezadrinst, branchinst, C, jmpinst, mp2_16b_1_p3, mp4_16b_1_p5, mp4_16b_2_p5, mp8_8b_1_p8,
       mp8_16b_1_p8, N, not_1_out, not_2_out, not_3_out, not_4_out, not_5_out, not_6_out, not_7_out,
       not_8_out, not_9_out, not_10_out, not_13_out, not_19_out, or_2_out, or_3_out, or_4_out, or_5_out,
       or_6_out, or_7_out, or_8_out, or_9_out, or_10_out, or_11_out, or_12_out, or_14_out, reg16_inc_ld_2_p4,
       rsff_2_p4, rsff_3_p4, rsff_5_p4, rsff_6_p4, rsff_7_p4, rsff_8_p4, rsff_9_p4, V, Z;
  wire [3:0] IR19__16, IR27__24;
  wire [7:0] DWH, DWL, IR7__0, IR15__8, PC7__0;
  wire [7:4] IR23__16, IR31__24;
  wire [15:0] ADDPCREL15__0, GPR15__0, mp4_16b_3_p5, SP15__0;
  wire [15:8] PC15__0;

  not not_1 (not_1_out, RST);
  not not_2 (not_2_out, RST);
  not not_3 (not_3_out, RST);
  // REG8_LD reg8_ld_1: pin names not known; wires that end beside it: CLK, not_3_out, MDR, {IR31__24, IR27__24}, CREGBUS[3]
  not not_4 (not_4_out, RST);
  // REG8_LD reg8_ld_2: pin names not known; wires that end beside it: CLK, not_4_out, MDR, {IR23__16, IR19__16}, CREGBUS[2]
  // DC4_16 dc4_16_1: pin names not known; wires that end beside it: IR31__24, PSW[0], bezadrinst, branchinst, jmpinst, adrinst
  // DC4_16 dc4_16_2: pin names not known; wires that end beside it: IR27__24, branchinst, INSTRUCBUS[8], INSTRUCBUS[9], INSTRUCBUS[10], INSTRUCBUS[11], INSTRUCBUS[12]
  // MP4_16b mp4_16b_1: pin names not known; wires that end beside it: CREGBUS[9], CREGBUS[8], {IR15__8, IR7__0}, GPR15__0, mp4_16b_1_p5, {DWH, DWL}, {{8{1'b0}}, MDR}, 1'b1
  // REG16 reg16_1: pin names not known; wires that end beside it: 1'b0, 1'b0, 1'b0, CLK, not_2_out, mp4_16b_1_p5, B, CREGBUS[4], CREGBUS[13], CREGBUS[14]
  // MP8_16b mp8_16b_1: pin names not known; wires that end beside it: CMEMBUS[7], CMEMBUS[6], CMEMBUS[5], {PC15__0, PC7__0}, {IR15__8, IR7__0}, GPR15__0, B, mp8_16b_1_p8, {DWH, DWL}, SP15__0, IVTPPDSP, 1'b1
  // REG16_INC_LD reg16_inc_ld_1: pin names not known; wires that end beside it: CLK, not_1_out, mp8_16b_1_p8, MAR, CMEMBUS[0], CMEMBUS[1]
  not not_5 (not_5_out, RST);
  not not_6 (not_6_out, RST);
  not not_7 (not_7_out, RST);
  // REG8_LD reg8_ld_3: pin names not known; wires that end beside it: CLK, not_6_out, MDR, IR15__8, CREGBUS[1]
  not not_8 (not_8_out, RST);
  // REG8_LD reg8_ld_4: pin names not known; wires that end beside it: CLK, not_8_out, MDR, IR7__0, CREGBUS[0]
  // DC4_16 dc4_16_3: pin names not known; wires that end beside it: IR27__24, bezadrinst, INSTRUCBUS[0], INSTRUCBUS[1], INSTRUCBUS[2], INSTRUCBUS[3], INSTRUCBUS[4], INSTRUCBUS[5], INSTRUCBUS[6], INSTRUCBUS[7]
  // DC4_16 dc4_16_4: pin names not known; wires that end beside it: IR27__24, jmpinst, INSTRUCBUS[13], INSTRUCBUS[14]
  // REG8_LD reg8_ld_5: pin names not known; wires that end beside it: CLK, not_7_out, MDR, DWH, CREGBUS[5]
  // ADD16 add16_1: pin names not known; wires that end beside it: {{9{IR23__16[7]}}, IR23__16[6:4], IR19__16}, ADDPCREL15__0, {PC15__0, PC7__0}, 1'b0
  // MP8_8b mp8_8b_1: pin names not known; wires that end beside it: CMEMBUS[8], CMEMBUS[9], CMEMBUS[10], DIN, A[15:8], A[7:0], PC7__0, mp8_8b_1_p8, PC15__0, {3'b000, PSW[4:0]}, {PSW[15], {7{1'b0}}}, 1'b1
  // REG8_LD reg8_ld_6: pin names not known; wires that end beside it: CLK, not_5_out, mp8_8b_1_p8, MDR, CMEMBUS[2]
  not not_9 (not_9_out, RST);
  // REG8_LD reg8_ld_7: pin names not known; wires that end beside it: CLK, not_9_out, MDR, DWL, CREGBUS[6]
  // MP4_16b mp4_16b_2: pin names not known; wires that end beside it: CMEMBUS[14], CMEMBUS[13], ADDPCREL15__0, {IR23__16, IR19__16, IR15__8}, mp4_16b_2_p5, {DWH, DWL}, 1'b1
  // DC4_16 dc4_16_5: pin names not known; wires that end beside it: IR27__24, adrinst, INSTRUCBUS[15], INSTRUCBUS[16], INSTRUCBUS[17], INSTRUCBUS[18], INSTRUCBUS[19], INSTRUCBUS[20]
  // DC4_16 dc4_16_6: pin names not known; wires that end beside it: IR23__16, adrinst, ADDRBUS[0], ADDRBUS[1], ADDRBUS[2], ADDRBUS[3], ADDRBUS[4], ADDRBUS[5], ADDRBUS[6]
  // REG16 reg16_2: pin names not known; wires that end beside it: CLK, 16'hf000, SP15__0, RST, CMEMBUS[11], CMEMBUS[12]
  not not_10 (not_10_out, RST);
  // RSFF rsff_1: pin names not known; wires that end beside it: CFFBUS[1], CLK, CFFBUS[0], not_10_out, PHASEFFBUS[0]
  // MP2_16b mp2_16b_1: pin names not known; wires that end beside it: RST, mp4_16b_2_p5, mp2_16b_1_p3, 16'h1000, 1'b1
  // REG16_INC_LD reg16_inc_ld_2: pin names not known; wires that end beside it: CLK, mp2_16b_1_p3, {PC15__0, PC7__0}, reg16_inc_ld_2_p4, CMEMBUS[4]
  or or_1 (reg16_inc_ld_2_p4, CMEMBUS[3], RST);
  // RSFF rsff_2: pin names not known; wires that end beside it: CFFBUS[3], CLK, CFFBUS[2], rsff_2_p4, PHASEFFBUS[1]
  not not_11 (rsff_2_p4, RST);
  // RSFF rsff_3: pin names not known; wires that end beside it: CFFBUS[5], CLK, CFFBUS[4], rsff_3_p4, PHASEFFBUS[2]
  not not_12 (rsff_3_p4, RST);
  and and_1 (and_1_out, CREGBUS[12], DWL[1]);
  and and_2 (and_2_out, CREGBUS[12], ~DWL[1]);  // AND_Gate
  and and_3 (and_3_out, CREGBUS[12], DWL[2]);
  and and_4 (and_4_out, CREGBUS[12], ~DWL[2]);  // AND_Gate
  and and_5 (and_5_out, CREGBUS[12], DWL[3]);
  and and_6 (and_6_out, CREGBUS[12], ~DWL[3]);  // AND_Gate
  and and_7 (and_7_out, CREGBUS[12], DWL[4]);
  and and_8 (and_8_out, CREGBUS[12], ~DWL[4]);  // AND_Gate
  and and_9 (and_9_out, ~DWL[0], INSTRUCBUS[2], CPSW[6]);  // AND_Gate
  or or_2 (or_2_out, and_9_out, CPSW[0]);
  and and_10 (and_10_out, DWL[0], INSTRUCBUS[2], CPSW[6]);
  and and_11 (and_11_out, CPSW[1], Z);
  and and_12 (and_12_out, CPSW[1], ~Z);  // AND_Gate
  and and_13 (and_13_out, CPSW[2], N);
  and and_14 (and_14_out, CPSW[2], ~N);  // AND_Gate
  and and_15 (and_15_out, CPSW[3], V);
  and and_16 (and_16_out, CPSW[3], ~V);  // AND_Gate
  and and_17 (and_17_out, CPSW[4], C);
  and and_18 (and_18_out, CPSW[4], ~C);  // AND_Gate
  and and_19 (and_19_out, CREGBUS[12], ~DWH[7]);  // AND_Gate
  and and_20 (and_20_out, CREGBUS[12], DWH[7]);
  // MP4_16b mp4_16b_3: pin names not known; wires that end beside it: CREGBUS[11], CREGBUS[10], B, A, mp4_16b_3_p5, 1'b1
  GPR16X16 gpr16x16_1 (
    .DI15__0(mp4_16b_3_p5), .A3__0(IR19__16), .WR(CREGBUS[7]), .CLK(CLK), .DO15__0(GPR15__0), .rst(RST));
  or or_3 (or_3_out, INSTRUCBUS[15], INSTRUCBUS[17], INSTRUCBUS[19], INSTRUCBUS[3], INSTRUCBUS[4]);
  and and_21 (and_21_out, ~A[8], ~A[9], ~A[10], ~A[11], ~A[12], ~A[13], ~A[14], ~A[15], ~A[0], ~A[1], ~A[2], ~A[3], ~A[4], ~A[5], ~A[6], ~A[7]);  // AND_Gate
  not not_13 (not_13_out, RST);
  // RSFF rsff_4: pin names not known; wires that end beside it: or_2_out, CLK, and_10_out, not_13_out, PSW[0]
  or or_4 (or_4_out, and_11_out, and_1_out);
  or or_5 (or_5_out, and_2_out, and_12_out);
  or or_6 (or_6_out, and_13_out, and_3_out);
  or or_7 (or_7_out, and_4_out, and_14_out);
  or or_8 (or_8_out, and_15_out, and_5_out);
  or or_9 (or_9_out, and_6_out, and_16_out);
  or or_10 (or_10_out, and_17_out, and_7_out);
  or or_11 (or_11_out, and_8_out, and_18_out);
  and and_22 (N, A[15], or_3_out);
  and and_23 (Z, or_3_out, and_21_out);
  // RSFF rsff_5: pin names not known; wires that end beside it: CFFBUS[7], CLK, CFFBUS[6], rsff_5_p4, PHASEFFBUS[3]
  not not_14 (rsff_5_p4, RST);
  // RSFF rsff_6: pin names not known; wires that end beside it: or_5_out, CLK, or_4_out, rsff_6_p4, PSW[1]
  not not_15 (rsff_6_p4, RST);
  // RSFF rsff_7: pin names not known; wires that end beside it: or_7_out, CLK, or_6_out, rsff_7_p4, PSW[2]
  not not_16 (rsff_7_p4, RST);
  // RSFF rsff_8: pin names not known; wires that end beside it: or_9_out, CLK, or_8_out, rsff_8_p4, PSW[3]
  not not_17 (rsff_8_p4, RST);
  // RSFF rsff_9: pin names not known; wires that end beside it: or_11_out, CLK, or_10_out, rsff_9_p4, PSW[4]
  not not_18 (rsff_9_p4, RST);
  not not_19 (not_19_out, RST);
  // RSFF rsff_10: pin names not known; wires that end beside it: and_19_out, CLK, and_20_out, not_19_out, PSW[15]
  or or_12 (or_12_out, INSTRUCBUS[3], INSTRUCBUS[4]);
  and and_24 (and_24_out, INSTRUCBUS[17], in_11);
  and and_25 (and_25_out, or_12_out, A[0]);
  and and_26 (and_26_out, ~A[15], ~B[15], ALU[15]);  // AND_Gate
  and and_27 (and_27_out, A[15], B[15], ~ALU[15]);  // AND_Gate
  or or_13 (C, and_24_out, and_25_out);
  or or_14 (or_14_out, and_26_out, and_27_out);
  and and_28 (V, INSTRUCBUS[17], or_14_out);

  assign PSW[14:5] = {10{1'b0}};

  // Other names for the same wires on the sheet: MDR7__0[7:0] = MDR; IR23__16[3:0] = IR19__16; A7__0[7:0] = A[7:0];
  //   A15__0[15:0] = A; A15__8[7:0] = A[15:8]; immed = ADDRBUS[0]; memdir = ADDRBUS[1]; memind = ADDRBUS[2];
  //   regind = ADDRBUS[3]; preincr = ADDRBUS[4]; postdec = ADDRBUS[5]; regdir = ADDRBUS[6]; ALU15__0[15:0] = ALU;
  //   B15__0[15:0] = B; C16 = in_11; stFETCH = CFFBUS[0]; clFETCH = CFFBUS[1]; stADDR = CFFBUS[2]; clADDR = CFFBUS[3];
  //   stEXEC = CFFBUS[4]; clEXEC = CFFBUS[5]; stINTR = CFFBUS[6]; clINTR = CFFBUS[7]; ldMAR = CMEMBUS[0];
  //   incMAR = CMEMBUS[1]; ldMDR = CMEMBUS[2]; ldPC = CMEMBUS[3]; incPC = CMEMBUS[4]; mxMAR0 = CMEMBUS[5];
  //   mxMAR1 = CMEMBUS[6]; mxMAR2 = CMEMBUS[7]; mxMDR2 = CMEMBUS[8]; mxMDR1 = CMEMBUS[9]; mxMDR0 = CMEMBUS[10];
  //   incSP = CMEMBUS[11]; decSP = CMEMBUS[12]; mxPC0 = CMEMBUS[13]; mxPC1 = CMEMBUS[14]; clPSWSTART = CPSW[0];
  //   ldZ = CPSW[1]; ldN = CPSW[2]; ldV = CPSW[3]; ldC = CPSW[4]; ldI = CPSW[5]; ldSTART = CPSW[6];
  //   ldIR7__0 = CREGBUS[0]; ldIR15__8 = CREGBUS[1]; ldIR23__16 = CREGBUS[2]; ldIR31__24 = CREGBUS[3];
  //   ldB = CREGBUS[4]; ldDWH = CREGBUS[5]; ldDWL = CREGBUS[6]; wrGPR = CREGBUS[7]; mxB0 = CREGBUS[8];
  //   mxB1 = CREGBUS[9]; mxGPR0 = CREGBUS[10]; mxGPR1 = CREGBUS[11]; ldPSW = CREGBUS[12]; incB = CREGBUS[13];
  //   decB = CREGBUS[14]; Din7__0[7:0] = DIN; ENTRADDR15__0[15:0] = IVTPPDSP; HALT = INSTRUCBUS[0];
  //   RTS = INSTRUCBUS[1]; RTI = INSTRUCBUS[2]; ROR = INSTRUCBUS[3]; RORC = INSTRUCBUS[4]; PUSHPSW = INSTRUCBUS[5];
  //   POPPSW = INSTRUCBUS[6]; STIVTP = INSTRUCBUS[7]; BGREU = INSTRUCBUS[8]; BLSSU = INSTRUCBUS[9];
  //   BLEQU = INSTRUCBUS[10]; JGRT = INSTRUCBUS[11]; JLEQ = INSTRUCBUS[12]; JMP = INSTRUCBUS[13];
  //   JSR = INSTRUCBUS[14]; LD = INSTRUCBUS[15]; ST = INSTRUCBUS[16]; ADD = INSTRUCBUS[17]; DEC = INSTRUCBUS[18];
  //   OR = INSTRUCBUS[19]; STRFIND = INSTRUCBUS[20]; IR31__24[3:0] = IR27__24; MAR15__0[15:0] = MAR;
  //   PC15__0[7:0] = PC7__0; PC15__8[7:0] = PC15__0; FETCH = PHASEFFBUS[0]; ADDR = PHASEFFBUS[1];
  //   EXEC = PHASEFFBUS[2]; INTR = PHASEFFBUS[3]; PSW7__0[4:0] = PSW[4:0]; PSWSTART = PSW[0]; PSWZ = PSW[1];
  //   PSWN = PSW[2]; PSWV = PSW[3]; PSWC = PSW[4]; PSW15__8[7] = PSW[15]; PSWI = PSW[15]

  // Notes on the sheet:
  //   Sabirac
  //   Instrukcijski registar
  //   Pomocni registri
  //   MAR
  //   Dekoderi za prepoznavanje instrukcije na osnovu sadrzaja registra IR31..24
  //   MDR
  //   SP
  //   Dekoderi za prepoznavanje nacina adresiranja
  //   PC
  //   FF za pokretanje FETCH, ADDR, EXEC i INTR faze izvršavanja instrukcije
  //   Registarski fajl
  //   Programska statusna reč (PSW)
endmodule

module FETCH (
  input  in_1,
  input  in_2,
  input  in_3,
  input  [3:0] PHASEFFBUS,
  input  [20:0] INSTRUCBUS,
  input  [6:0] ADDRBUS,
  input  [15:0] PSW,
  output [14:0] CMEMBUS,
  output [7:0] CFFBUS,
  output [14:0] CREGBUS,
  output rdMEM
);

  wire addr2, addr_t, and_2_out, and_3_out, and_4_out, and_5_out, and_6_out, and_7_out, and_8_out, and_9_out,
       and_10_out, and_11_out, bezadr1, bradr2, brbezadr1, brbrnch2, brcnd, brgrinst, brjmp3, brnch2,
       brnotfcmem, brnotPSWSTARTandFETCH, bruncnd, clFETCH, grinst, incPC, jmp3, ldIR7__0, ldIR15__8,
       ldIR23__16, ldIR31__24, ldMAR, ldMDR, not_1_out, not_3_out, or_5_out, or_7_out, rdMEM_t,
       reg8_inc_ld_1_p5, reg8_inc_ld_1_p6, stADDR, stEXEC;
  wire [7:0] reg8_inc_ld_1_p4;
  wire [23:11] rom256x24_1_dout;

  or or_1 (bezadr1, INSTRUCBUS[0], INSTRUCBUS[1], INSTRUCBUS[3], INSTRUCBUS[2], INSTRUCBUS[4], INSTRUCBUS[5], INSTRUCBUS[6], INSTRUCBUS[7]);
  or or_2 (brnch2, INSTRUCBUS[8], INSTRUCBUS[9], INSTRUCBUS[10]);
  or or_3 (jmp3, INSTRUCBUS[11], INSTRUCBUS[12], INSTRUCBUS[13], INSTRUCBUS[14]);
  not not_1 (not_1_out, in_1);
  // REG8_INC_LD reg8_inc_ld_1: pin names not known; wires that end beside it: in_2, not_1_out, rom256x24_1_dout[23:16], reg8_inc_ld_1_p4, reg8_inc_ld_1_p5, reg8_inc_ld_1_p6
  not not_2 (reg8_inc_ld_1_p6, reg8_inc_ld_1_p5);
  // DC4_16 dc4_16_1: pin names not known; wires that end beside it: rom256x24_1_dout[15:12], 1'b1, bradr2, bruncnd, brnotPSWSTARTandFETCH, brnotfcmem, brbezadr1, brbrnch2, brjmp3, brgrinst
  or or_4 (reg8_inc_ld_1_p5, bruncnd, brcnd);
  ROM256X24 rom256x24_1 (
    .A7__0(reg8_inc_ld_1_p4), .CS(1'b1),
    .DOUT({rom256x24_1_dout, stEXEC, stADDR, clFETCH, ldIR7__0, ldIR15__8, ldIR23__16, ldIR31__24, ldMDR, rdMEM_t, incPC, ldMAR}));
  or or_5 (or_5_out, ADDRBUS[3], ADDRBUS[4], ADDRBUS[6], ADDRBUS[5]);
  or or_6 (addr_t, INSTRUCBUS[15], INSTRUCBUS[16], INSTRUCBUS[17], INSTRUCBUS[18], INSTRUCBUS[19], INSTRUCBUS[20]);
  and and_1 (addr2, or_5_out, addr_t);
  or or_7 (or_7_out, ~PHASEFFBUS[0], ~PSW[0]);  // OR_Gate
  not not_3 (not_3_out, in_3);
  and and_2 (and_2_out, ~bezadr1, ~jmp3, ~brnch2, ~addr_t);  // AND_Gate
  and and_3 (and_3_out, addr_t, ~ADDRBUS[3], ~ADDRBUS[4], ~ADDRBUS[6], ~ADDRBUS[5], ~ADDRBUS[0], ~ADDRBUS[1], ~ADDRBUS[2]);  // AND_Gate
  and and_4 (and_4_out, INSTRUCBUS[16], ADDRBUS[0]);
  and and_5 (and_5_out, or_7_out, brnotPSWSTARTandFETCH);
  and and_6 (and_6_out, brbezadr1, bezadr1);
  and and_7 (and_7_out, brjmp3, jmp3);
  and and_8 (and_8_out, brnch2, brbrnch2);
  and and_9 (and_9_out, bradr2, addr2);
  and and_10 (and_10_out, brnotfcmem, not_3_out);
  and and_11 (and_11_out, brgrinst, grinst);
  or or_8 (grinst, and_2_out, and_3_out, and_4_out);
  or or_9 (brcnd, and_5_out, and_6_out, and_7_out, and_8_out, and_9_out, and_10_out, and_11_out);
  assign CMEMBUS[0] = ldMAR ? 1'b1 : 1'bz;  // Controlled_Buffer controlled_buffer_1
  assign CMEMBUS[2] = ldMDR ? 1'b1 : 1'bz;  // Controlled_Buffer controlled_buffer_2
  assign CMEMBUS[4] = incPC ? 1'b1 : 1'bz;  // Controlled_Buffer controlled_buffer_3
  assign CFFBUS[1] = clFETCH ? 1'b1 : 1'bz;  // Controlled_Buffer controlled_buffer_4
  assign CFFBUS[2] = stADDR ? 1'b1 : 1'bz;  // Controlled_Buffer controlled_buffer_5
  assign CFFBUS[4] = stEXEC ? 1'b1 : 1'bz;  // Controlled_Buffer controlled_buffer_6
  assign CREGBUS[0] = ldIR7__0 ? 1'b1 : 1'bz;  // Controlled_Buffer controlled_buffer_7
  assign CREGBUS[1] = ldIR15__8 ? 1'b1 : 1'bz;  // Controlled_Buffer controlled_buffer_8
  assign CREGBUS[2] = ldIR23__16 ? 1'b1 : 1'bz;  // Controlled_Buffer controlled_buffer_9
  assign CREGBUS[3] = ldIR31__24 ? 1'b1 : 1'bz;  // Controlled_Buffer controlled_buffer_10
  assign rdMEM = rdMEM_t ? 1'b1 : 1'bz;  // Controlled_Buffer controlled_buffer_11

  // Other names for the same wires on the sheet: immed = ADDRBUS[0]; memdir = ADDRBUS[1]; memind = ADDRBUS[2];
  //   regind = ADDRBUS[3]; preincr = ADDRBUS[4]; postdec = ADDRBUS[5]; regdir = ADDRBUS[6]; CLK = in_2; FCBUS = in_3;
  //   HALT = INSTRUCBUS[0]; RTS = INSTRUCBUS[1]; RTI = INSTRUCBUS[2]; ROR = INSTRUCBUS[3]; RORC = INSTRUCBUS[4];
  //   PUSHPSW = INSTRUCBUS[5]; POPPSW = INSTRUCBUS[6]; STIVTP = INSTRUCBUS[7]; BGREU = INSTRUCBUS[8];
  //   BLSSU = INSTRUCBUS[9]; BLEQU = INSTRUCBUS[10]; JGRT = INSTRUCBUS[11]; JLEQ = INSTRUCBUS[12];
  //   JMP = INSTRUCBUS[13]; JSR = INSTRUCBUS[14]; LD = INSTRUCBUS[15]; ST = INSTRUCBUS[16]; ADD = INSTRUCBUS[17];
  //   DEC = INSTRUCBUS[18]; OR = INSTRUCBUS[19]; STRFIND = INSTRUCBUS[20]; FETCH = PHASEFFBUS[0];
  //   ADDR = PHASEFFBUS[1]; EXEC = PHASEFFBUS[2]; INTR = PHASEFFBUS[3]; PSWSTART = PSW[0]; rst = in_1

  // Notes on the sheet:
  //   Operaciona jedinica
  //   Operaciona jedinica
  //   Kontrolna jedinica
  //   Kontrolna jedinica
endmodule

module ADDR (
  input  in_1,
  input  in_2,
  input  in_3,
  input  [3:0] PHASEFFBUS,
  input  [20:0] INSTRUCBUS,
  input  [6:0] ADDRBUS,
  output [14:0] CMEMBUS,
  output [7:0] CFFBUS,
  output [14:0] CREGBUS,
  output rdMEM
);

  wire and_1_out, and_2_out, and_3_out, bradr, brcnd, brnotADDR, brnotfcbus, brSTORE, bruncnd, clADDR, decB,
       incB, incMAR, ldB, ldDWH, ldDWL, ldMAR, ldMDR, mp2_8b_1_p3, mxB0, mxB1, mxMAR0, mxMAR1, mxMAR2,
       not_1_out, not_3_out, not_4_out, rdMEM_t, reg8_inc_ld_1_p6, reg8_inc_ld_1_p7, stEXEC, wrGPR;
  wire [2:0] dc3_8_1_p1;
  wire [7:0] mp2_8b_1_p2, mp2_8b_1_p4, reg8_inc_ld_1_p5;
  wire [23:17] rom256x32_addr_1_dout;

  // MP2_8b mp2_8b_1: pin names not known; wires that end beside it: bradr, mp2_8b_1_p2, mp2_8b_1_p3, mp2_8b_1_p4, 1'b1
  not not_1 (not_1_out, in_1);
  // DC3_8 dc3_8_1: pin names not known; wires that end beside it: dc3_8_1_p1, 1'b1, bruncnd, brnotADDR, brSTORE, brnotfcbus, bradr
  KMADDR kmaddr_1 (
    .immed(ADDRBUS[0]), .memdir(ADDRBUS[1]), .memind(ADDRBUS[2]), .regind(ADDRBUS[3]), .preincr(ADDRBUS[4]),
    .postdecr(ADDRBUS[5]), .regdir(ADDRBUS[6]), .ADR7__0(mp2_8b_1_p4));
  // REG8_INC_LD reg8_inc_ld_1: pin names not known; wires that end beside it: 1'b0, in_2, not_1_out, mp2_8b_1_p3, reg8_inc_ld_1_p5, reg8_inc_ld_1_p6, reg8_inc_ld_1_p7
  not not_2 (reg8_inc_ld_1_p7, reg8_inc_ld_1_p6);
  or or_1 (reg8_inc_ld_1_p6, bruncnd, brcnd, bradr);
  ROM256X32_ADDR rom256x32_addr_1 (
    .A7__0(reg8_inc_ld_1_p5), .CS(1'b1),
    .DOUT({mp2_8b_1_p2, rom256x32_addr_1_dout[23], dc3_8_1_p1, rom256x32_addr_1_dout[19:17], incB, stEXEC, clADDR, mxB1, wrGPR, decB, mxB0, mxMAR1, mxMAR2, ldDWL, incMAR, ldDWH, ldMDR, rdMEM_t, mxMAR0, ldMAR, ldB}));
  not not_3 (not_3_out, PHASEFFBUS[1]);
  not not_4 (not_4_out, in_3);
  and and_1 (and_1_out, not_3_out, brnotADDR);
  and and_2 (and_2_out, INSTRUCBUS[16], brSTORE);
  and and_3 (and_3_out, brnotfcbus, not_4_out);
  or or_2 (brcnd, and_1_out, and_2_out, and_3_out);
  assign CMEMBUS[0] = ldMAR ? 1'b1 : 1'bz;  // Controlled_Buffer controlled_buffer_1
  assign CMEMBUS[1] = incMAR ? 1'b1 : 1'bz;  // Controlled_Buffer controlled_buffer_2
  assign CMEMBUS[2] = ldMDR ? 1'b1 : 1'bz;  // Controlled_Buffer controlled_buffer_3
  assign CMEMBUS[5] = mxMAR0 ? 1'b1 : 1'bz;  // Controlled_Buffer controlled_buffer_4
  assign CMEMBUS[6] = mxMAR1 ? 1'b1 : 1'bz;  // Controlled_Buffer controlled_buffer_5
  assign CMEMBUS[7] = mxMAR2 ? 1'b1 : 1'bz;  // Controlled_Buffer controlled_buffer_6
  assign CFFBUS[3] = clADDR ? 1'b1 : 1'bz;  // Controlled_Buffer controlled_buffer_7
  assign CFFBUS[4] = stEXEC ? 1'b1 : 1'bz;  // Controlled_Buffer controlled_buffer_8
  assign CREGBUS[4] = ldB ? 1'b1 : 1'bz;  // Controlled_Buffer controlled_buffer_9
  assign CREGBUS[5] = ldDWH ? 1'b1 : 1'bz;  // Controlled_Buffer controlled_buffer_10
  assign CREGBUS[6] = ldDWL ? 1'b1 : 1'bz;  // Controlled_Buffer controlled_buffer_11
  assign CREGBUS[7] = wrGPR ? 1'b1 : 1'bz;  // Controlled_Buffer controlled_buffer_12
  assign CREGBUS[8] = mxB0 ? 1'b1 : 1'bz;  // Controlled_Buffer controlled_buffer_13
  assign CREGBUS[9] = mxB1 ? 1'b1 : 1'bz;  // Controlled_Buffer controlled_buffer_14
  assign CREGBUS[14] = decB ? 1'b1 : 1'bz;  // Controlled_Buffer controlled_buffer_15
  assign CREGBUS[13] = incB ? 1'b1 : 1'bz;  // Controlled_Buffer controlled_buffer_16
  assign rdMEM = rdMEM_t ? 1'b1 : 1'bz;  // Controlled_Buffer controlled_buffer_17

  // Other names for the same wires on the sheet: immed = ADDRBUS[0]; memdir = ADDRBUS[1]; memind = ADDRBUS[2];
  //   regind = ADDRBUS[3]; preincr = ADDRBUS[4]; postdec = ADDRBUS[5]; regdir = ADDRBUS[6]; CLK = in_2; FCBUS = in_3;
  //   ST = INSTRUCBUS[16]; FETCH = PHASEFFBUS[0]; ADDR = PHASEFFBUS[1]; EXEC = PHASEFFBUS[2]; INTR = PHASEFFBUS[3];
  //   rst = in_1

  // Notes on the sheet:
  //   Operaciona jedinica
  //   Upravljacka jedinica
endmodule

module EXEC (
  input  in_1,
  input  in_2,
  input  in_3,
  input  [15:0] B,
  input  [3:0] PHASEFFBUS,
  input  [20:0] INSTRUCBUS,
  input  [6:0] ADDRBUS,
  input  [15:0] PSW,
  output [15:0] A,
  output [15:0] ALU,
  output C16,
  output [14:0] CMEMBUS,
  output [7:0] CFFBUS,
  output [14:0] CREGBUS,
  output [6:0] CPSW,
  output rdMEM,
  output wrMEM,
  output ldIVTP
);

  wire A_B, add_t, and_1_out, and_2_out, and_3_out, and_4_out, and_5_out, and_6_out, and_7_out, and_8_out,
       and_9_out, and_10_out, brA_B, brcnd, brnotEXEC, brnotFCBUS, brorjmp, brregdir, bruncnd, \case , clCNT,
       clEXEC, clPSWSTART, decB, decSP, incCNT, incMAR, incSP, ldA, ldB, ldC, ldDWH, ldDWL, ldIVTP_t, ldMAR,
       ldMDR, ldN, ldPC, ldPSW, ldV, ldZ, mp2_1b_1_p3, mp2_8b_1_p3, mp2_16b_1_p3, mxA, mxB0, mxB1, mxGPR0,
       mxIR, mxMAR0, mxMAR1, mxMAR2, mxMDR0, mxMDR1, mxMDR2, mxPC0, mxPC1, not_1_out, not_3_out, not_4_out,
       not_5_out, notbropr, or_2_out, or_3_out, or_t, rdMEM_t, reg8_inc_ld_1_p5, reg8_inc_ld_1_p6, srA,
       stINTR, wrGPR, wrMEM_t, xor_1_out;
  wire [2:0] dc3_8_1_p1;
  wire [7:0] mp2_8b_1_p2, mp2_8b_1_p4, reg8_inc_ld_1_p4;
  wire [15:0] CNT15__0;
  wire [31:9] rom_256x64_1_dout63__32;

  // MP2_1b mp2_1b_1: pin names not known; wires that end beside it: mxIR, A[0], mp2_1b_1_p3, PSW[4], 1'b1
  // MP2_16b mp2_16b_1: pin names not known; wires that end beside it: mxA, B, mp2_16b_1_p3, ALU, 1'b1
  // REG16 reg16_1: pin names not known; wires that end beside it: in_1, srA, mp2_1b_1_p3, in_2, 1'b1, mp2_16b_1_p3, A, ldA, 1'b0, 1'b0, 1'b0, 1'b0
  not not_1 (not_1_out, in_1);
  // DC3_8 dc3_8_1: pin names not known; wires that end beside it: dc3_8_1_p1, 1'b1, brnotFCBUS, brA_B, notbropr, \case , bruncnd, brnotEXEC, brregdir
  // MP2_8b mp2_8b_1: pin names not known; wires that end beside it: \case , mp2_8b_1_p2, mp2_8b_1_p3, mp2_8b_1_p4, 1'b1
  // REG8_INC_LD reg8_inc_ld_1: pin names not known; wires that end beside it: in_2, not_1_out, mp2_8b_1_p3, reg8_inc_ld_1_p4, reg8_inc_ld_1_p5, reg8_inc_ld_1_p6
  not not_2 (reg8_inc_ld_1_p6, reg8_inc_ld_1_p5);
  or or_1 (reg8_inc_ld_1_p5, bruncnd, brcnd, \case );
  ROM_256X64 rom_256x64_1 (
    .A7__0(reg8_inc_ld_1_p4), .CS(1'b1),
    .DOUT63__32({rom_256x64_1_dout63__32[31:24], mp2_8b_1_p2, rom_256x64_1_dout63__32[15], dc3_8_1_p1, rom_256x64_1_dout63__32[11:9], mxMAR1, stINTR, clEXEC, clPSWSTART, ldIVTP_t, ldPSW, incCNT, clCNT, mxB1}),
    .DOUT31__0({mxB0, ldB, decB, mxGPR0, wrMEM_t, rdMEM_t, wrGPR, or_t, add_t, ldDWH, ldDWL, mxPC1, mxPC0, ldPC, decSP, incSP, ldC, ldV, ldZ, ldN, incMAR, mxMAR2, mxMAR0, ldMAR, mxMDR2, mxMDR1, mxMDR0, ldMDR, mxIR, srA, mxA, ldA}));
  ALU16 alu16_1 (.Cin(1'b0), .A(A), .B(B), .add(add_t), .sub(1'b0), .\or (or_t), .F(ALU), .Cout(C16));
  KMEXEC kmexec_1 (
    .LD(INSTRUCBUS[15]), .ST(INSTRUCBUS[16]), .ADD(INSTRUCBUS[17]), .DEC(INSTRUCBUS[18]),
    .OR(INSTRUCBUS[19]), .ROR(INSTRUCBUS[3]), .RORC(INSTRUCBUS[4]), .STRFIND(INSTRUCBUS[20]),
    .BGREU(INSTRUCBUS[8]), .BLSSU(INSTRUCBUS[9]), .BLEQU(INSTRUCBUS[10]), .JGRT(INSTRUCBUS[11]),
    .JLEQ(INSTRUCBUS[12]), .JMP(INSTRUCBUS[13]), .JSR(INSTRUCBUS[14]), .PUSHPSW(INSTRUCBUS[5]),
    .POPPSW(INSTRUCBUS[6]), .STIVTP(INSTRUCBUS[7]), .RTS(INSTRUCBUS[1]), .RTI(INSTRUCBUS[2]),
    .HALT(INSTRUCBUS[0]), .out_22(mp2_8b_1_p4));
  or or_2 (or_2_out, PSW[4], PSW[1]);
  xor xor_1 (xor_1_out, PSW[2], PSW[3]);
  and and_1 (and_1_out, or_2_out, INSTRUCBUS[10]);
  or or_3 (or_3_out, PSW[1], xor_1_out);
  and and_2 (and_2_out, ~PSW[4], INSTRUCBUS[8]);  // AND_Gate
  and and_3 (and_3_out, PSW[4], INSTRUCBUS[9]);
  and and_4 (and_4_out, or_3_out, INSTRUCBUS[12]);
  and and_5 (and_5_out, ~or_3_out, INSTRUCBUS[11]);  // AND_Gate
  not not_3 (not_3_out, PHASEFFBUS[2]);
  and and_6 (and_6_out, brA_B, A_B);
  and and_7 (and_7_out, notbropr, ~brorjmp);  // AND_Gate
  not not_4 (not_4_out, in_3);
  or or_4 (brorjmp, and_2_out, and_3_out, and_1_out, and_5_out, and_4_out);
  and and_8 (and_8_out, not_3_out, brnotEXEC);
  and and_9 (and_9_out, brregdir, ADDRBUS[6]);
  and and_10 (and_10_out, not_4_out, brnotFCBUS);
  assign ldIVTP = ldIVTP_t ? 1'b1 : 1'bz;  // Controlled_Buffer controlled_buffer_1
  or or_5 (brcnd, and_8_out, and_9_out, and_6_out, and_7_out, and_10_out);
  Comparator comparator_1 (.a(B[7:0]), .b(A[7:0]), .eq(A_B));  // open: gt, lt
  not not_5 (not_5_out, in_1);
  assign CMEMBUS[6] = mxMAR1 ? 1'b1 : 1'bz;  // Controlled_Buffer controlled_buffer_2
  assign CMEMBUS[7] = mxMAR2 ? 1'b1 : 1'bz;  // Controlled_Buffer controlled_buffer_3
  assign CMEMBUS[9] = mxMDR1 ? 1'b1 : 1'bz;  // Controlled_Buffer controlled_buffer_4
  assign CMEMBUS[11] = incSP ? 1'b1 : 1'bz;  // Controlled_Buffer controlled_buffer_5
  assign CMEMBUS[12] = decSP ? 1'b1 : 1'bz;  // Controlled_Buffer controlled_buffer_6
  assign CREGBUS[4] = ldB ? 1'b1 : 1'bz;  // Controlled_Buffer controlled_buffer_7
  assign CREGBUS[5] = ldDWH ? 1'b1 : 1'bz;  // Controlled_Buffer controlled_buffer_8
  assign CREGBUS[6] = ldDWL ? 1'b1 : 1'bz;  // Controlled_Buffer controlled_buffer_9
  assign CREGBUS[7] = wrGPR ? 1'b1 : 1'bz;  // Controlled_Buffer controlled_buffer_10
  assign CREGBUS[8] = mxB0 ? 1'b1 : 1'bz;  // Controlled_Buffer controlled_buffer_11
  assign CREGBUS[9] = mxB1 ? 1'b1 : 1'bz;  // Controlled_Buffer controlled_buffer_12
  assign CREGBUS[10] = mxGPR0 ? 1'b1 : 1'bz;  // Controlled_Buffer controlled_buffer_13
  assign CPSW[1] = ldZ ? 1'b1 : 1'bz;  // Controlled_Buffer controlled_buffer_14
  assign CPSW[2] = ldN ? 1'b1 : 1'bz;  // Controlled_Buffer controlled_buffer_15
  // REG16 reg16_2: pin names not known; wires that end beside it: clCNT, 1'b0, 1'b0, in_2, not_5_out, CNT15__0, 1'b0, 1'b0, 1'b0, incCNT, 1'b0
  assign CMEMBUS[8] = mxMDR2 ? 1'b1 : 1'bz;  // Controlled_Buffer controlled_buffer_16
  assign CMEMBUS[10] = mxMDR0 ? 1'b1 : 1'bz;  // Controlled_Buffer controlled_buffer_17
  assign CPSW[3] = ldV ? 1'b1 : 1'bz;  // Controlled_Buffer controlled_buffer_18
  assign CPSW[4] = ldC ? 1'b1 : 1'bz;  // Controlled_Buffer controlled_buffer_19
  assign CMEMBUS[5] = mxMAR0 ? 1'b1 : 1'bz;  // Controlled_Buffer controlled_buffer_20
  assign CREGBUS[12] = ldPSW ? 1'b1 : 1'bz;  // Controlled_Buffer controlled_buffer_21
  assign CPSW[0] = clPSWSTART ? 1'b1 : 1'bz;  // Controlled_Buffer controlled_buffer_22
  assign CMEMBUS[3] = ldPC ? 1'b1 : 1'bz;  // Controlled_Buffer controlled_buffer_23
  assign CFFBUS[5] = clEXEC ? 1'b1 : 1'bz;  // Controlled_Buffer controlled_buffer_24
  assign CFFBUS[6] = stINTR ? 1'b1 : 1'bz;  // Controlled_Buffer controlled_buffer_25
  assign CMEMBUS[1] = incMAR ? 1'b1 : 1'bz;  // Controlled_Buffer controlled_buffer_26
  assign CMEMBUS[2] = ldMDR ? 1'b1 : 1'bz;  // Controlled_Buffer controlled_buffer_27
  assign CMEMBUS[13] = mxPC0 ? 1'b1 : 1'bz;  // Controlled_Buffer controlled_buffer_28
  assign CMEMBUS[14] = mxPC1 ? 1'b1 : 1'bz;  // Controlled_Buffer controlled_buffer_29
  assign rdMEM = rdMEM_t ? 1'b1 : 1'bz;  // Controlled_Buffer controlled_buffer_30
  assign wrMEM = wrMEM_t ? 1'b1 : 1'bz;  // Controlled_Buffer controlled_buffer_31
  assign CMEMBUS[0] = ldMAR ? 1'b1 : 1'bz;  // Controlled_Buffer controlled_buffer_32
  assign CREGBUS[14] = decB ? 1'b1 : 1'bz;  // Controlled_Buffer controlled_buffer_33

  // Other names for the same wires on the sheet: A7__0[7:0] = A[7:0]; A15__0[15:0] = A; regdir = ADDRBUS[6];
  //   ALU15__0[15:0] = ALU; B7__0[7:0] = B[7:0]; B15__0[15:0] = B; CLK = in_2; FCBUS = in_3; HALT = INSTRUCBUS[0];
  //   RTS = INSTRUCBUS[1]; RTI = INSTRUCBUS[2]; ROR = INSTRUCBUS[3]; RORC = INSTRUCBUS[4]; PUSHPSW = INSTRUCBUS[5];
  //   POPPSW = INSTRUCBUS[6]; STIVTP = INSTRUCBUS[7]; BGREU = INSTRUCBUS[8]; BLSSU = INSTRUCBUS[9];
  //   BLEQU = INSTRUCBUS[10]; JGRT = INSTRUCBUS[11]; JLEQ = INSTRUCBUS[12]; JMP = INSTRUCBUS[13];
  //   JSR = INSTRUCBUS[14]; LD = INSTRUCBUS[15]; ST = INSTRUCBUS[16]; ADD = INSTRUCBUS[17]; DEC = INSTRUCBUS[18];
  //   OR = INSTRUCBUS[19]; STRFIND = INSTRUCBUS[20]; EXEC = PHASEFFBUS[2]; PSWZ = PSW[1]; PSWN = PSW[2];
  //   PSWV = PSW[3]; PSWC = PSW[4]; rst = in_1

  // Notes on the sheet:
  //   Operaciona jedinica
  //   Operaciona jedinica
  //   Akumulator
  //   ALU
  //   Uslov za skok
endmodule

module INTR (
  input  in_1,
  input  in_2,
  input  in_3,
  input  [15:0] A15__0,
  input  [3:0] PHASEFFBUS,
  input  [20:0] INSTRUCBUS,
  input  [15:0] PSW,
  input  [3:0] intr,
  input  in_9,
  output [15:0] ADDIVTP,
  output [1:0] UEXT1__0,
  output inta,
  output [14:0] CMEMBUS,
  output [7:0] CFFBUS,
  output [14:0] CREGBUS,
  output rdMEM,
  output wrMEM
);

  wire and_2_out, and_3_out, and_4_out, brcnd, brnotFCBUS, brnotINTR, brnotprekid, bruncnd, clINTR, decSP,
       incMAR, ldDWH, ldDWL, ldMAR, ldMDR, ldPC, mxMAR0, mxMAR1, mxMAR2, mxMDR0, mxMDR1, mxMDR2, mxPC1,
       not_1_out, not_2_out, not_3_out, not_5_out, not_6_out, not_7_out, prekid, prper, rdMEM_t,
       reg8_inc_ld_1_p5, reg8_inc_ld_1_p6, stFETCH, wrMEM_t;
  wire [2:0] dc3_8_1_p1;
  wire [2:1] IVTDSP15__0;
  wire [7:0] reg8_inc_ld_1_p3, reg8_inc_ld_1_p4;
  wire [15:0] IVTP15__0;
  wire [23:19] rom256x32_intr_1_dout;

  and and_1 (prekid, prper, PSW[15], not_2_out);
  not not_1 (not_1_out, in_1);
  // REG8_INC_LD reg8_inc_ld_1: pin names not known; wires that end beside it: in_2, not_1_out, reg8_inc_ld_1_p3, reg8_inc_ld_1_p4, reg8_inc_ld_1_p5, reg8_inc_ld_1_p6
  // DC3_8 dc3_8_1: pin names not known; wires that end beside it: dc3_8_1_p1, 1'b1, bruncnd, brnotINTR, brnotprekid, brnotFCBUS
  not not_2 (not_2_out, INSTRUCBUS[0]);
  not not_3 (not_3_out, in_1);
  // REG16_LD reg16_ld_1: pin names not known; wires that end beside it: in_2, not_3_out, A15__0, IVTP15__0, in_9
  not not_4 (reg8_inc_ld_1_p6, reg8_inc_ld_1_p5);
  ROM256X32_INTR rom256x32_intr_1 (
    .A7__0(reg8_inc_ld_1_p4), .CS(1'b1),
    .DOUT({reg8_inc_ld_1_p3, rom256x32_intr_1_dout[23], dc3_8_1_p1, rom256x32_intr_1_dout[19], clINTR, stFETCH, mxPC1, ldPC, ldDWH, ldDWL, incMAR, rdMEM_t, mxMAR2, inta, mxMDR2, mxMDR0, wrMEM_t, ldMDR, mxMDR1, decSP, ldMAR, mxMAR1, mxMAR0}));
  or or_1 (prper, intr[3], intr[2], intr[1], intr[0]);
  or or_2 (reg8_inc_ld_1_p5, bruncnd, brcnd);
  // CD4 cd4_1: pin names not known; wires that end beside it: intr[3], intr[2], intr[1], intr[0], 1'b1, UEXT1__0[1], UEXT1__0[0]
  // REG2_LD reg2_ld_1: pin names not known; wires that end beside it: in_2, UEXT1__0, IVTDSP15__0, inta
  // ADD16 add16_1: pin names not known; wires that end beside it: IVTP15__0, ADDIVTP, {{13{1'b0}}, IVTDSP15__0, 1'b0}, 1'b0
  not not_5 (not_5_out, PHASEFFBUS[3]);
  not not_6 (not_6_out, prekid);
  not not_7 (not_7_out, in_3);
  and and_2 (and_2_out, not_5_out, brnotINTR);
  and and_3 (and_3_out, not_6_out, brnotprekid);
  and and_4 (and_4_out, not_7_out, brnotFCBUS);
  or or_3 (brcnd, and_2_out, and_3_out, and_4_out);
  assign CMEMBUS[0] = ldMAR ? 1'b1 : 1'bz;  // Controlled_Buffer controlled_buffer_1
  assign CMEMBUS[1] = incMAR ? 1'b1 : 1'bz;  // Controlled_Buffer controlled_buffer_2
  assign CMEMBUS[2] = ldMDR ? 1'b1 : 1'bz;  // Controlled_Buffer controlled_buffer_3
  assign CMEMBUS[3] = ldPC ? 1'b1 : 1'bz;  // Controlled_Buffer controlled_buffer_4
  assign CMEMBUS[5] = mxMAR0 ? 1'b1 : 1'bz;  // Controlled_Buffer controlled_buffer_5
  assign CMEMBUS[6] = mxMAR1 ? 1'b1 : 1'bz;  // Controlled_Buffer controlled_buffer_6
  assign CMEMBUS[7] = mxMAR2 ? 1'b1 : 1'bz;  // Controlled_Buffer controlled_buffer_7
  assign CMEMBUS[8] = mxMDR2 ? 1'b1 : 1'bz;  // Controlled_Buffer controlled_buffer_8
  assign CMEMBUS[9] = mxMDR1 ? 1'b1 : 1'bz;  // Controlled_Buffer controlled_buffer_9
  assign CMEMBUS[10] = mxMDR0 ? 1'b1 : 1'bz;  // Controlled_Buffer controlled_buffer_10
  assign CFFBUS[0] = stFETCH ? 1'b1 : 1'bz;  // Controlled_Buffer controlled_buffer_11
  assign CFFBUS[7] = clINTR ? 1'b1 : 1'bz;  // Controlled_Buffer controlled_buffer_12
  assign CREGBUS[5] = ldDWH ? 1'b1 : 1'bz;  // Controlled_Buffer controlled_buffer_13
  assign CREGBUS[6] = ldDWL ? 1'b1 : 1'bz;  // Controlled_Buffer controlled_buffer_14
  assign CMEMBUS[12] = decSP ? 1'b1 : 1'bz;  // Controlled_Buffer controlled_buffer_15
  assign CMEMBUS[14] = mxPC1 ? 1'b1 : 1'bz;  // Controlled_Buffer controlled_buffer_16
  assign rdMEM = rdMEM_t ? 1'b1 : 1'bz;  // Controlled_Buffer controlled_buffer_17
  assign wrMEM = wrMEM_t ? 1'b1 : 1'bz;  // Controlled_Buffer controlled_buffer_18

  // Other names for the same wires on the sheet: ldBR = inta; ADDIVTP15__0[15:0] = ADDIVTP; CLK = in_2; FCBUS = in_3;
  //   HALT = INSTRUCBUS[0]; intr3__0[3:0] = intr; ldIVTP = in_9; INTR_t = PHASEFFBUS[3]; PSWI = PSW[15]; rst = in_1

  // Notes on the sheet:
  //   Operaciona jedinica
  //   Upravljacka jedinica
endmodule

module RAM (
  input  [15:0] in_1,
  input  in_2,
  input  [7:0] in_3,
  input  in_4,
  input  in_5,
  input  in_6,
  output [7:0] out_7,
  output out_8
);

  wire and_1_out, and_2_out, CNT0, LDCNT, not_1_out, notCNT0, or_1_out, reg4_ld_sl_sr_1_p6, rsff_2_p4,
       rsff_2_p5, rsff_3_p4, sl;
  wire [3:0] CNT, LFSR;

  // RSFF rsff_1: pin names not known; wires that end beside it: 1'b0, in_2, in_6, sl
  or or_1 (or_1_out, in_4, in_5);
  // REG4_LD_SL_SR reg4_ld_sl_sr_1: pin names not known; wires that end beside it: 1'b0, 1'b0, in_2, 4'b1111, LFSR, reg4_ld_sl_sr_1_p6, sl, in_6
  // RisingEdge risingedge_1: pin names not known; wires that end beside it: or_1_out, in_2, LDCNT
  // MEM64Kx8 mem64kx8_1: pin names not known; wires that end beside it: in_1, 1'b1, in_2, in_3, out_7, in_4
  xor xor_1 (reg4_ld_sl_sr_1_p6, LFSR[2], LFSR[3]);
  and and_1 (and_1_out, CNT0, not_1_out);
  not not_1 (not_1_out, LDCNT);
  // RSFF rsff_2: pin names not known; wires that end beside it: and_1_out, in_2, LDCNT, rsff_2_p4, rsff_2_p5
  not not_2 (rsff_2_p4, in_6);
  and and_2 (and_2_out, rsff_2_p5, CNT0);
  // REG4m_DEC_LD reg4m_dec_ld_1: pin names not known; wires that end beside it: in_2, LFSR, CNT, LDCNT, notCNT0, notCNT0
  or or_2 (notCNT0, CNT[0], CNT[1], CNT[2], CNT[3]);
  // RSFF rsff_3: pin names not known; wires that end beside it: out_8, in_2, and_2_out, rsff_3_p4, out_8
  not not_3 (rsff_3_p4, in_6);
  not not_4 (CNT0, notCNT0);

  // Other names for the same wires on the sheet: ADR[15:0] = in_1; CLK = in_2; DIN[7:0] = in_3; DOUT[7:0] = out_7;
  //   fc = out_8; RDMEM = in_5; rst = in_6; WRMEM = in_4

  // Notes on the sheet:
  //   Random broj predstavlja vreme pristupa memoriji
  //   Brojac za generisanje random broja 
  //   Jedinica za generisanje function complete (fc) signala
  //   Brojac za dekrementiranje random broja
endmodule
