// Logisim project ETFStudent.circ as structural Verilog: 13 circuits, main circuit KMADR
module REG32_LD (
  input  [31:0] I15__0,
  input  LD,
  input  mr,
  input  CLK,
  output [31:0] A15__0
);

  // REG16_LD reg16_ld_1: pin names not known; wires that end beside it: CLK, mr, I15__0[31:16], A15__0[31:16], LD
  // REG16_LD reg16_ld_2: pin names not known; wires that end beside it: CLK, mr, I15__0[15:0], A15__0[15:0], LD

  // Notes on the sheet:
  //   __
endmodule

module KMADR (
  input  immed,
  input  memdir,
  input  regdir,
  input  regindpom,
  output [3:0] Adr3__0
);

  assign Adr3__0 = immed ? 4'b0010 : 4'bz;  // Controlled_Buffer controlled_buffer_1
  assign Adr3__0 = memdir ? 4'b0100 : 4'bz;  // Controlled_Buffer controlled_buffer_2
  assign Adr3__0 = regdir ? 4'b0101 : 4'bz;  // Controlled_Buffer controlled_buffer_3
  assign Adr3__0 = regindpom ? 4'b0111 : 4'bz;  // Controlled_Buffer controlled_buffer_4
endmodule

module KMOPR (
  input  LD,
  input  ST,
  input  ADD,
  input  SUB,
  input  BLSS,
  input  JLEQ,
  input  JMP,
  input  JSR,
  input  RTS,
  input  RTI,
  input  HALT,
  output [5:0] Adr5__0
);

  assign Adr5__0 = LD ? 6'b000010 : 6'bz;  // Controlled_Buffer controlled_buffer_1
  assign Adr5__0 = ST ? 6'b000100 : 6'bz;  // Controlled_Buffer controlled_buffer_2
  assign Adr5__0 = ADD ? 6'b001010 : 6'bz;  // Controlled_Buffer controlled_buffer_3
  assign Adr5__0 = SUB ? 6'b001100 : 6'bz;  // Controlled_Buffer controlled_buffer_4
  assign Adr5__0 = BLSS ? 6'b001110 : 6'bz;  // Controlled_Buffer controlled_buffer_5
  assign Adr5__0 = JLEQ ? 6'b010000 : 6'bz;  // Controlled_Buffer controlled_buffer_6
  assign Adr5__0 = JMP ? 6'b010001 : 6'bz;  // Controlled_Buffer controlled_buffer_7
  assign Adr5__0 = JSR ? 6'b010010 : 6'bz;  // Controlled_Buffer controlled_buffer_8
  assign Adr5__0 = RTS ? 6'b010111 : 6'bz;  // Controlled_Buffer controlled_buffer_9
  assign Adr5__0 = RTI ? 6'b011110 : 6'bz;  // Controlled_Buffer controlled_buffer_10
  assign Adr5__0 = HALT ? 6'b100010 : 6'bz;  // Controlled_Buffer controlled_buffer_11
endmodule

module REG6_INC_LD (
  input  [5:0] I5__0,
  input  LD,
  input  INC,
  input  mr,
  input  CLK,
  output [5:0] A5__0
);

  wire reg2m_inc_ld_1_p7, reg2m_inc_ld_2_p8;

  // REG2m_INC_LD reg2m_inc_ld_1: pin names not known; wires that end beside it: CLK, mr, I5__0[5:4], A5__0[5:4], LD, INC, reg2m_inc_ld_1_p7
  // REG2m_INC_LD reg2m_inc_ld_2: pin names not known; wires that end beside it: CLK, reg2m_inc_ld_1_p7, mr, I5__0[3:2], A5__0[3:2], LD, INC, reg2m_inc_ld_2_p8
  // REG2m_INC_LD reg2m_inc_ld_3: pin names not known; wires that end beside it: CLK, reg2m_inc_ld_2_p8, mr, I5__0[1:0], A5__0[1:0], LD, INC, INC

  // Notes on the sheet:
  //   __
endmodule

module ROM256X24 (
  input  [7:0] A7__0,
  input  CS,
  output [23:0] DOUT
);

  ROM #(.dataWidth(24)) rom_1 (.addr(A7__0), .data(DOUT), .sel(CS));
endmodule

module GPR16X16 (
  input  [15:0] DI15__0,
  input  [3:0] A3__0,
  input  WR,
  input  CLK,
  input  rst,
  output [15:0] DO15__0
);

  wire and_6_out, and_11_out, CS0, CS1, CS2, CS3, CS4, CS5, CS6, CS7, CS8, CS9, CS10, CS11, CS12, CS13, CS14,
       CS15, not_1_out, not_2_out, not_3_out, not_4_out, not_5_out, not_6_out, not_7_out, not_8_out,
       not_9_out, not_10_out, not_11_out, not_12_out, not_13_out, not_14_out, not_15_out, not_16_out,
       reg16_ld_1_p5, reg16_ld_2_p5, reg16_ld_3_p5, reg16_ld_4_p5, reg16_ld_5_p5, reg16_ld_7_p5,
       reg16_ld_8_p5, reg16_ld_9_p5, reg16_ld_10_p5, reg16_ld_12_p5, reg16_ld_13_p5, reg16_ld_14_p5,
       reg16_ld_15_p5, reg16_ld_16_p5;
  wire [15:0] reg16_ld_1_p4, reg16_ld_2_p4, reg16_ld_3_p4, reg16_ld_4_p4, reg16_ld_5_p4, reg16_ld_6_p4,
       reg16_ld_7_p4, reg16_ld_8_p4, reg16_ld_9_p4, reg16_ld_10_p4, reg16_ld_11_p4, reg16_ld_12_p4,
       reg16_ld_13_p4, reg16_ld_14_p4, reg16_ld_15_p4, reg16_ld_16_p4;

  // DC4_16 dc4_16_1: pin names not known; wires that end beside it: A3__0, 1'b1, CS0, CS1, CS2, CS3, CS4, CS5, CS6, CS7, CS8, CS9, CS10, CS11, CS12, CS13, CS14, CS15
  not not_1 (not_1_out, rst);
  // REG16_LD reg16_ld_1: pin names not known; wires that end beside it: CLK, not_1_out, DI15__0, reg16_ld_1_p4, reg16_ld_1_p5
  assign DO15__0 = CS0 ? reg16_ld_1_p4 : 16'bz;  // Controlled_Buffer controlled_buffer_1
  not not_2 (not_2_out, rst);
  // REG16_LD reg16_ld_2: pin names not known; wires that end beside it: CLK, not_2_out, DI15__0, reg16_ld_2_p4, reg16_ld_2_p5
  assign DO15__0 = CS1 ? reg16_ld_2_p4 : 16'bz;  // Controlled_Buffer controlled_buffer_2
  not not_3 (not_3_out, rst);
  // REG16_LD reg16_ld_3: pin names not known; wires that end beside it: CLK, not_3_out, DI15__0, reg16_ld_3_p4, reg16_ld_3_p5
  assign DO15__0 = CS2 ? reg16_ld_3_p4 : 16'bz;  // Controlled_Buffer controlled_buffer_3
  not not_4 (not_4_out, rst);
  // REG16_LD reg16_ld_4: pin names not known; wires that end beside it: CLK, not_4_out, DI15__0, reg16_ld_4_p4, reg16_ld_4_p5
  assign DO15__0 = CS3 ? reg16_ld_4_p4 : 16'bz;  // Controlled_Buffer controlled_buffer_4
  and and_1 (reg16_ld_1_p5, CS0, WR);
  and and_2 (reg16_ld_2_p5, CS1, WR);
  and and_3 (reg16_ld_3_p5, CS2, WR);
  and and_4 (reg16_ld_4_p5, CS3, WR);
  not not_5 (not_5_out, rst);
  not not_6 (not_6_out, rst);
  not not_7 (not_7_out, rst);
  not not_8 (not_8_out, rst);
  // REG16_LD reg16_ld_5: pin names not known; wires that end beside it: CLK, not_5_out, DI15__0, reg16_ld_5_p4, reg16_ld_5_p5
  and and_5 (reg16_ld_5_p5, CS4, WR);
  assign DO15__0 = CS4 ? reg16_ld_5_p4 : 16'bz;  // Controlled_Buffer controlled_buffer_5
  and and_6 (and_6_out, CS5, WR);
  // REG16_LD reg16_ld_6: pin names not known; wires that end beside it: CLK, not_6_out, DI15__0, reg16_ld_6_p4, and_6_out
  assign DO15__0 = CS5 ? reg16_ld_6_p4 : 16'bz;  // Controlled_Buffer controlled_buffer_6
  // REG16_LD reg16_ld_7: pin names not known; wires that end beside it: CLK, not_7_out, DI15__0, reg16_ld_7_p4, reg16_ld_7_p5
  and and_7 (reg16_ld_7_p5, CS6, WR);
  assign DO15__0 = CS6 ? reg16_ld_7_p4 : 16'bz;  // Controlled_Buffer controlled_buffer_7
  // REG16_LD reg16_ld_8: pin names not known; wires that end beside it: CLK, not_8_out, DI15__0, reg16_ld_8_p4, reg16_ld_8_p5
  and and_8 (reg16_ld_8_p5, CS7, WR);
  assign DO15__0 = CS7 ? reg16_ld_8_p4 : 16'bz;  // Controlled_Buffer controlled_buffer_8
  not not_9 (not_9_out, rst);
  not not_10 (not_10_out, rst);
  not not_11 (not_11_out, rst);
  not not_12 (not_12_out, rst);
  // REG16_LD reg16_ld_9: pin names not known; wires that end beside it: CLK, not_9_out, DI15__0, reg16_ld_9_p4, reg16_ld_9_p5
  and and_9 (reg16_ld_9_p5, CS8, WR);
  assign DO15__0 = CS8 ? reg16_ld_9_p4 : 16'bz;  // Controlled_Buffer controlled_buffer_9
  // REG16_LD reg16_ld_10: pin names not known; wires that end beside it: CLK, not_10_out, DI15__0, reg16_ld_10_p4, reg16_ld_10_p5
  and and_10 (reg16_ld_10_p5, CS9, WR);
  assign DO15__0 = CS9 ? reg16_ld_10_p4 : 16'bz;  // Controlled_Buffer controlled_buffer_10
  and and_11 (and_11_out, CS10, WR);
  // REG16_LD reg16_ld_11: pin names not known; wires that end beside it: CLK, not_11_out, DI15__0, reg16_ld_11_p4, and_11_out
  assign DO15__0 = CS10 ? reg16_ld_11_p4 : 16'bz;  // Controlled_Buffer controlled_buffer_11
  // REG16_LD reg16_ld_12: pin names not known; wires that end beside it: CLK, not_12_out, DI15__0, reg16_ld_12_p4, reg16_ld_12_p5
  and and_12 (reg16_ld_12_p5, CS11, WR);
  assign DO15__0 = CS11 ? reg16_ld_12_p4 : 16'bz;  // Controlled_Buffer controlled_buffer_12
  not not_13 (not_13_out, rst);
  // REG16_LD reg16_ld_13: pin names not known; wires that end beside it: CLK, not_13_out, DI15__0, reg16_ld_13_p4, reg16_ld_13_p5
  assign DO15__0 = CS12 ? reg16_ld_13_p4 : 16'bz;  // Controlled_Buffer controlled_buffer_13
  not not_14 (not_14_out, rst);
  // REG16_LD reg16_ld_14: pin names not known; wires that end beside it: CLK, not_14_out, DI15__0, reg16_ld_14_p4, reg16_ld_14_p5
  assign DO15__0 = CS13 ? reg16_ld_14_p4 : 16'bz;  // Controlled_Buffer controlled_buffer_14
  not not_15 (not_15_out, rst);
  // REG16_LD reg16_ld_15: pin names not known; wires that end beside it: CLK, not_15_out, DI15__0, reg16_ld_15_p4, reg16_ld_15_p5
  assign DO15__0 = CS14 ? reg16_ld_15_p4 : 16'bz;  // Controlled_Buffer controlled_buffer_15
  not not_16 (not_16_out, rst);
  // REG16_LD reg16_ld_16: pin names not known; wires that end beside it: CLK, not_16_out, DI15__0, reg16_ld_16_p4, reg16_ld_16_p5
  assign DO15__0 = CS15 ? reg16_ld_16_p4 : 16'bz;  // Controlled_Buffer controlled_buffer_16
  and and_13 (reg16_ld_13_p5, CS12, WR);
  and and_14 (reg16_ld_14_p5, CS13, WR);
  and and_15 (reg16_ld_15_p5, CS14, WR);
  and and_16 (reg16_ld_16_p5, CS15, WR);

  // Other names for the same wires on the sheet: inREG[15:0] = DI15__0; outREG[15:0] = DO15__0
endmodule

module KMADDR (
  input  immed,
  input  memdir,
  input  memind,
  input  regind,
  input  preincr,
  input  postdecr,
  input  regdir,
  output [7:0] ADR7__0
);

  assign ADR7__0 = immed ? 8'h2 : 8'bz;  // Controlled_Buffer controlled_buffer_1
  assign ADR7__0 = memdir ? 8'h3 : 8'bz;  // Controlled_Buffer controlled_buffer_2
  assign ADR7__0 = memind ? 8'h4 : 8'bz;  // Controlled_Buffer controlled_buffer_3
  assign ADR7__0 = regind ? 8'ha : 8'bz;  // Controlled_Buffer controlled_buffer_4
  assign ADR7__0 = preincr ? 8'hb : 8'bz;  // Controlled_Buffer controlled_buffer_5
  assign ADR7__0 = postdecr ? 8'hf : 8'bz;  // Controlled_Buffer controlled_buffer_6
  assign ADR7__0 = regdir ? 8'h13 : 8'bz;  // Controlled_Buffer controlled_buffer_7
endmodule

module ALU16 (
  input  Cin,
  input  [15:0] A,
  input  [15:0] B,
  input  add,
  input  sub,
  input  \or ,
  output [15:0] F,
  output Cout
);

  wire adder_1_cout, subtractor_1_bout;
  wire [15:0] adder_1_out, or_1_out, subtractor_1_out;

  Adder #(.width(16)) adder_1 (.a(A), .b(B), .out(adder_1_out), .cin(Cin), .cout(adder_1_cout));
  Subtractor #(.width(16)) subtractor_1 (.a(A), .b(B), .out(subtractor_1_out), .bin(Cin), .bout(subtractor_1_bout));
  assign or_1_out = A | B;  // OR_Gate or_1, 16 bits wide
  assign F = add ? adder_1_out : 16'bz;  // Controlled_Buffer controlled_buffer_1
  assign Cout = add ? adder_1_cout : 1'bz;  // Controlled_Buffer controlled_buffer_2
  assign F = sub ? subtractor_1_out : 16'bz;  // Controlled_Buffer controlled_buffer_3
  assign Cout = sub ? subtractor_1_bout : 1'bz;  // Controlled_Buffer controlled_buffer_4
  assign F = \or  ? or_1_out : 16'bz;  // Controlled_Buffer controlled_buffer_5
endmodule

module KMEXEC (
  input  STRFIND,
  input  JSR,
  input  PUSHPSW,
  input  POPPSW,
  input  STIVTP,
  input  RTS,
  input  RTI,
  input  HALT,
  input  JLEQ,
  input  JMP,
  input  LD,
  input  ST,
  input  ADD,
  input  DEC,
  input  OR,
  input  ROR,
  input  RORC,
  input  BGREU,
  input  BLSSU,
  input  BLEQU,
  input  JGRT,
  output [7:0] out_22
);

  assign out_22 = LD ? 8'h2 : 8'bz;  // Controlled_Buffer controlled_buffer_1
  assign out_22 = ST ? 8'h4 : 8'bz;  // Controlled_Buffer controlled_buffer_2
  assign out_22 = ADD ? 8'hb : 8'bz;  // Controlled_Buffer controlled_buffer_3
  assign out_22 = DEC ? 8'hd : 8'bz;  // Controlled_Buffer controlled_buffer_4
  assign out_22 = OR ? 8'he : 8'bz;  // Controlled_Buffer controlled_buffer_5
  assign out_22 = ROR ? 8'h10 : 8'bz;  // Controlled_Buffer controlled_buffer_6
  assign out_22 = RORC ? 8'h12 : 8'bz;  // Controlled_Buffer controlled_buffer_7
  assign out_22 = STRFIND ? 8'h14 : 8'bz;  // Controlled_Buffer controlled_buffer_8
  assign out_22 = BGREU ? 8'h19 : 8'bz;  // Controlled_Buffer controlled_buffer_9
  assign out_22 = BLSSU ? 8'h1b : 8'bz;  // Controlled_Buffer controlled_buffer_10
  assign out_22 = BLEQU ? 8'h1d : 8'bz;  // Controlled_Buffer controlled_buffer_11
  assign out_22 = JGRT ? 8'h1f : 8'bz;  // Controlled_Buffer controlled_buffer_12
  assign out_22 = JLEQ ? 8'h21 : 8'bz;  // Controlled_Buffer controlled_buffer_13
  assign out_22 = JMP ? 8'h24 : 8'bz;  // Controlled_Buffer controlled_buffer_14
  assign out_22 = JSR ? 8'h25 : 8'bz;  // Controlled_Buffer controlled_buffer_15
  assign out_22 = PUSHPSW ? 8'h2a : 8'bz;  // Controlled_Buffer controlled_buffer_16
  assign out_22 = POPPSW ? 8'h2f : 8'bz;  // Controlled_Buffer controlled_buffer_17
  assign out_22 = STIVTP ? 8'h37 : 8'bz;  // Controlled_Buffer controlled_buffer_18
  assign out_22 = RTS ? 8'h38 : 8'bz;  // Controlled_Buffer controlled_buffer_19
  assign out_22 = RTI ? 8'h40 : 8'bz;  // Controlled_Buffer controlled_buffer_20
  assign out_22 = HALT ? 8'h51 : 8'bz;  // Controlled_Buffer controlled_buffer_21
endmodule

module ROM_256X64 (
  input  [7:0] A7__0,
  input  CS,
  output [31:0] DOUT63__32,
  output [31:0] DOUT31__0
);

  ROM #(.dataWidth(32)) rom_1 (.addr(A7__0), .data(DOUT63__32), .sel(CS));
  ROM #(.dataWidth(32)) rom_2 (.addr(A7__0), .data(DOUT31__0), .sel(CS));
endmodule

module ROM256X28 (
  input  [7:0] A7__0,
  input  CS,
  output [27:0] DOUT
);

  ROM #(.dataWidth(28)) rom_1 (.addr(A7__0), .data(DOUT), .sel(CS));
endmodule

module ROM256X32_INTR (
  input  [7:0] A7__0,
  input  CS,
  output [31:0] DOUT
);

  ROM #(.dataWidth(32)) rom_1 (.addr(A7__0), .data(DOUT), .sel(CS));
endmodule

module ROM256X32_ADDR (
  input  [7:0] A7__0,
  input  CS,
  output [31:0] DOUT
);

  ROM #(.dataWidth(32)) rom_1 (.addr(A7__0), .data(DOUT), .sel(CS));
endmodule
